# Fritzing sketch led_strip_pir_rotary_encoder (saved by Fritzing 0.9.3b)
breadboards: 1

parts:
  Součástka1 = Arduino Uno (Rev3)
  PIR1 = PIR sensor
  U1 = WS2812 RGB LED strip
  ENCODER2 = Rotary Encoder with switch (KY-040) [part_number=KY-040]

nets:
  N1: Součástka1.D2, PIR1.SIG
  N2: Součástka1.D3_PWM, ENCODER2.SW
  N3: Součástka1.D4, ENCODER2.CLK
  N4: Součástka1.D5_PWM, ENCODER2.DT
  N5: Součástka1.D6_PWM, U1.DIN
  5V: Součástka1.5V, PIR1.VDD, U1.VCC, ENCODER2.+
  GND: Součástka1.GND, PIR1.GND, U1.GND, ENCODER2.GND

custom parts:
  WS2812 RGB LED strip: WS2812 strip
  Rotary Encoder with switch (KY-040): A Rotary Encoder with switch
